# Fritzing sketch LED (saved by Fritzing 0.9.3b)
stripboards: 1

parts:
  J1 = female pin header, 3 pins [form="♀ (female)"]
  R1 = Resistor [tolerance=±5% resistance=2.2 package="2512 [SMD]"]
  Q1 = NPN-Transistor [package="TO92 [THT]"]
  R2 = Resistor [tolerance=±5% resistance=2.2 package="2512 [SMD]"]
  LED1 = smd LED [color="Infrared (850nm)" package="0805 [SMD]"]
  LED2 = smd LED [color="Infrared (850nm)" package="0805 [SMD]"]
  LED3 = smd LED [color="Infrared (850nm)" package="0805 [SMD]"]

nets:
  N1: J1.pin1, Q1.C
  N2: J1.pin2, R1.Pin_0
  N3: J1.pin3, R2.Pin_0
  N4: R1.Pin_1, Q1.B
  N5: Q1.E, LED1.anode
  N6: R2.Pin_1, LED3.cathode
  N7: LED1.cathode, LED2.anode
  N8: LED2.cathode, LED3.anode

notes:
  5V
  GPIO
  GND
