# Fritzing sketch distribution_board (saved by Fritzing 0.9.3b)
stripboards: 1

parts:
  J1 = double row male pin header, 6 pins [form="♂ (male)"]
  J2 = male pin header, 3 pins [form="♂ (male)"]
  J3 = male pin header, 3 pins [form="♂ (male)"]
  J4 = male pin header, 3 pins [form="♂ (male)"]
  J5 = male pin header, 4 pins [form="♂ (male)"]
  J6 = male pin header, 3 pins [form="♂ (male)"]
  J7 = male pin header, 2 pins [form="♂ (male)"]
  Part1 = Adafruit Pi Cobbler [part_number="Adafruit #914"]
  J8 = male pin header, 3 pins [form="♂ (male)"]
  J9 = male pin header, 3 pins [form="♂ (male)"]

nets:
  N1: J1.pin1, J5.pin1, J6.pin3, J7.pin2, Part1.3.3V
  N2: J1.pin2, Part1.SCLK
  N3: J1.pin3, Part1.MISO
  N4: J1.pin4, Part1.MOSI
  N5: J1.pin5, Part1.CE0
  N6: J1.pin6, J2.pin3, J3.pin3, J4.pin3, J5.pin2, J6.pin1, J7.pin1, Part1.GND, J8.pin3, J9.pin3
  N7: J2.pin1, Part1.RXD
  N8: J2.pin2, Part1.TXD
  N9: J3.pin1, J4.pin1, Part1.5.0V, J8.pin1, J9.pin1
  N10: J3.pin2, J4.pin2, Part1.GPIO23
  N11: J6.pin2, Part1.GPIO25
  N12: Part1.GPIO17, J8.pin2, J9.pin2

notes:
  MISO
  GND
  MOSI
  SCLK
  3V3
  CS
  TX
  RX
  GPIO
  5V
  SCL
  SDA
  Force Sensor
  Temp/Humidity
  IR Beam
  IR LEDs
  UART

custom parts:
  Adafruit Pi Cobbler: Now that you've finally got your hands on a Raspberry Pi® Model B , you're probably itching to make some fun embedded computer projects with it. What you need is an add on prototyping Pi Cobbler from Adafruit, which can break out all those tasty power, GPIO, I2C and SPI pins from the 26 pin header onto a solderless breadboard. This set will make "cobbling together" prototypes with the Pi super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
