# Fritzing sketch force_sensor (saved by Fritzing 0.9.3b)
stripboards: 2

parts:
  R1 = Trimmer Potentiometer [maximum_resistance=100kΩ package=THT]
  J2 = Basic Force Sensing Resistor (FSR) [package=THT]  # not connected
  IC1 = MCP3008 8-channel 10-bit ADC [part_number=MCP3008]
  J4 = male pin header, 6 pins [form="♂ (male)"]
  J5 = female pin header, 2 pins [form="♀ (female)"]
  J6 = Screw terminal - 2 pins [package=THT]
  J7 = female pin header, 2 pins [form="♀ (female)"]

nets:
  N1: R1.leg1, IC1.no_name_yet#2
  N2: R1.wiper, IC1.no_name_yet#1, J5.pin1, J6.pin1, J7.pin2
  N3: R1.leg2, IC1.no_name_yet#15, IC1.no_name_yet#16, J4.pin1
  N4: IC1.no_name_yet#9, IC1.no_name_yet#14, J4.pin6, J5.pin2, J6.pin2, J7.pin1
  N5: IC1.no_name_yet#10, J4.pin5
  N6: IC1.no_name_yet#11, J4.pin4
  N7: IC1.no_name_yet#12, J4.pin3
  N8: IC1.no_name_yet#13, J4.pin2

notes:
  3V3
  MOSI
  MISO
  SCLK
  GND
  CS
