# Fritzing sketch distribution_board (saved by Fritzing 0.9.3b)
stripboards: 1

parts:
  J1 = double row male pin header, 6 pins [form="♂ (male)"]
  J2 = male pin header, 3 pins [form="♂ (male)"]  # not connected
  J3 = male pin header, 3 pins [form="♂ (male)"]
  J4 = male pin header, 3 pins [form="♂ (male)"]
  J5 = male pin header, 4 pins [form="♂ (male)"]
  J6 = male pin header, 3 pins [form="♂ (male)"]
  J7 = male pin header, 2 pins [form="♂ (male)"]
  Part1 = Adafruit Pi Cobbler [part_number="Adafruit #914"]  # not connected
  J8 = male pin header, 3 pins [form="♂ (male)"]
  J9 = male pin header, 3 pins [form="♂ (male)"]

nets:
  N1: J1.pin1, J6.pin3, J7.pin2
  N2: J1.pin6, J6.pin1, J7.pin1
  N3: J3.pin1, J4.pin1, J8.pin1, J9.pin1
  N4: J3.pin2, J4.pin2
  N5: J4.pin3, J5.pin2, J8.pin3, J9.pin3
  N6: J8.pin2, J9.pin2

notes:
  MISO
  GND
  MOSI
  SCLK
  3V3
  CS
  TX
  RX
  GPIO
  5V
  SCL
  SDA
  Force Sensor
  Temp/Humidity
  IR Beam
  IR LEDs
  UART

custom parts:
  Adafruit Pi Cobbler: Now that you've finally got your hands on a Raspberry Pi® Model B , you're probably itching to make some fun embedded computer projects with it. What you need is an add on prototyping Pi Cobbler from Adafruit, which can break out all those tasty power, GPIO, I2C and SPI pins from the 26 pin header onto a solderless breadboard. This set will make "cobbling together" prototypes with the Pi super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
