# Fritzing sketch power_board (saved by Fritzing 0.9.3b)
stripboards: 1

parts:
  J1 = female pin header, 4 pins [form="♀ (female)"]
  J2 = female pin header, 3 pins [form="♀ (female)"]
  J3 = female pin header, 2 pins [form="♀ (female)"]

nets:
  N1: J1.pin1, J2.pin1
  N2: J1.pin4, J2.pin2, J3.pin1
  N3: J2.pin3, J3.pin2

notes:
  GND
  5V
  19.5V
  Buck Converter
  |
  Female USB
